# Fritzing sketch fritzing role (saved by Fritzing 0.9.3b)

parts:
  Parça1 = Arduino Uno (Rev3)
  U1 = 2-Channel 5v Relay Shield [package=relay-2ch5v10a]
  LED1 = LEDs [package=led10mm]
  VCC1 = Battery block 9V

nets:
  N1: Parça1.D8, U1.IN1
  5V: Parça1.5V, U1.VCC
  GND: Parça1.GND, U1.GND
  N2: U1.K1-In, LED1.C
  N3: U1.K1-On, VCC1.+

custom parts:
  2-Channel 5v Relay Shield: 2 Channel 5v Relay Shield w. 2x SPD-06VDC-SD-C
  LEDs: LEDs Standard schematic elements and footprints for 5mm, 3mm, 1206, and 0603 sized LEDs. 5mm - Spark Fun Electronics SKU : COM-00529 (and others)
